// Digital circuit RealTimeClock_Wrong.dig as structural Verilog
module RealTimeClock_Wrong (
  input  clk
);

  wire and_1_out, counterpreset_2_ovf, counterpreset_3_ovf, counterpreset_4_ovf, counterpreset_5_ovf,
       counterpreset_6_ovf, counterpreset_7_ovf, counterpreset_8_ovf;
  wire [3:0] counterpreset_1_out, counterpreset_2_out, counterpreset_4_out, counterpreset_5_out,
       counterpreset_7_out, counterpreset_8_out;

  CounterPreset #(.maxValue(2), .Bits(4)) counterpreset_1 (
    .en(counterpreset_2_ovf), .C(clk), .dir(1'b0), .in(4'b0000), .ld(1'b0), .clr(counterpreset_3_ovf),
    .out(counterpreset_1_out));  // open: ovf
  CounterPreset #(.maxValue(9), .Bits(4)) counterpreset_2 (
    .en(counterpreset_4_ovf), .C(clk), .dir(1'b0), .in(4'b0000), .ld(1'b0), .clr(counterpreset_3_ovf),
    .out(counterpreset_2_out), .ovf(counterpreset_2_ovf));
  and and_1 (and_1_out, counterpreset_6_ovf, counterpreset_4_ovf);
  CounterPreset #(.maxValue(23), .Bits(6)) counterpreset_3 (
    .en(and_1_out), .C(clk), .dir(1'b0), .in({6{1'b0}}), .ld(1'b0), .clr(1'b0), .ovf(counterpreset_3_ovf));  // open: out
  CounterPreset #(.maxValue(5), .Bits(4)) counterpreset_4 (
    .en(counterpreset_5_ovf), .C(clk), .dir(1'b0), .in(4'b0000), .ld(1'b0), .clr(1'b0),
    .out(counterpreset_4_out), .ovf(counterpreset_4_ovf));
  Seven_Seg_Hex seven_seg_hex_1 (.d(counterpreset_1_out), .dp(1'b0));
  CounterPreset #(.maxValue(9), .Bits(4)) counterpreset_5 (
    .en(counterpreset_7_ovf), .C(clk), .dir(1'b0), .in(4'b0000), .ld(1'b0), .clr(1'b0),
    .out(counterpreset_5_out), .ovf(counterpreset_5_ovf));
  Seven_Seg_Hex seven_seg_hex_2 (.d(counterpreset_2_out), .dp(1'b0));
  CounterPreset #(.maxValue(49), .Bits(6)) counterpreset_6 (
    .en(1'b1), .C(clk), .dir(1'b0), .in({6{1'b0}}), .ld(1'b0), .clr(1'b0), .ovf(counterpreset_6_ovf));  // open: out
  Seven_Seg_Hex seven_seg_hex_3 (.d(counterpreset_4_out), .dp(1'b0));
  CounterPreset #(.maxValue(5), .Bits(4)) counterpreset_7 (
    .en(counterpreset_8_ovf), .C(clk), .dir(1'b0), .in(4'b0000), .ld(1'b0), .clr(1'b0),
    .out(counterpreset_7_out), .ovf(counterpreset_7_ovf));
  Seven_Seg_Hex seven_seg_hex_4 (.d(counterpreset_5_out), .dp(1'b0));
  CounterPreset #(.maxValue(9), .Bits(4)) counterpreset_8 (
    .en(counterpreset_6_ovf), .C(clk), .dir(1'b0), .in(4'b0000), .ld(1'b0), .clr(1'b0),
    .out(counterpreset_8_out), .ovf(counterpreset_8_ovf));
  Seven_Seg_Hex seven_seg_hex_5 (.d(counterpreset_7_out), .dp(1'b0));
  Seven_Seg_Hex seven_seg_hex_6 (.d(counterpreset_8_out), .dp(1'b0));

  // Notes on the sheet:
  //   clk: Hz: 500000
endmodule
